# Fritzing sketch Workflow2 (saved by Fritzing 0.9.3b)
breadboards: 1

parts:
  Part1 = Arduino Uno (Rev3)
  R1 = PHOTOCELL [package=photocell-kit]
  R2 = Resistor [tolerance=±5% resistance=10k package=THT]
  VCC1 = Battery block 9V  # not connected
  Part2 = Adafruit Ultimate GPS Logger Shield [part_number="Adafruit #1272"]
  T1 = TMP36 Temperature Sensor [package="TO92 [THT]"]
  S1 = Pushbutton [package="[THT]"]
  R3 = Resistor [tolerance=±5% resistance=10k package=THT]

nets:
  N1: Part1.A0, R1.P$1, R2.Pin_1, Part2.A0
  N2: Part1.A1, Part2.A1, T1.Vout
  N3: Part1.A2, Part2.A2
  N4: Part1.A3, Part2.A3
  N5: Part1.A4/SDA, Part2.A4, Part2.SDA
  N6: Part1.A5/SCL, Part2.A5, Part2.SCL
  N7: Part1.D8, Part2.D8
  N8: Part1.D9_PWM, Part2.D9
  N9: Part1.D10_PWM/SS, Part2.SD_CS
  N10: Part1.D11_PWM/MOSI, Part2.MOSI
  N11: Part1.D12/MISO, Part2.MISO
  N12: Part1.D13/SCK, Part2.SCK
  GND: Part1.GND, R1.P$2, Part2.GND, T1.GND, R3.Pin_1
  N13: Part1.AREF, Part2.AREF
  N14: Part1.D0/RX, Part2.D0
  N15: Part1.D1/TX, Part2.D1
  N16: Part1.D2, Part2.D2
  N17: Part1.D3_PWM, Part2.D3
  N18: Part1.D4, Part2.D4
  N19: Part1.D5_PWM, Part2.D5, S1.Pin_1, S1.Pin_2, R3.Pin_0
  N20: Part1.D6_PWM, Part2.D6
  N21: Part1.D7, Part2.D7
  N22: Part1.ioref, Part2.IOREF
  N23: Part1.RESET, Part2.RESET
  N24: Part1.3V3, Part2.3V
  5V: Part1.5V, R2.Pin_0, Part2.+5V, T1.+Vs, S1.Pin_3, S1.Pin_4
  VIN: Part1.VIN, Part2.VIN
  N25: Part1.N/C, Part2.NC

custom parts:
  Adafruit Ultimate GPS Logger Shield: Brand new and better than ever, we've replaced our Adafruit GPS shield kit with this assembled shield that comes with an Ultimate GPS module. This GPS shield works great with either UNO or Leonardo Arduinos and is designed to log data to an SD card. Or you can leave the SD card out and use the GPS for a geocaching project, or maybe a music player that changes tunes depending on where you are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
